# Fritzing sketch adept-schematic (saved by Fritzing 0.9.2b)
breadboards: 1

parts:
  IC1 = IC, DIP package, 16 pins [chip_label=INA125P]
  R1 = Resistor [tolerance=±5% resistance=1k package=THT]
  Part1 = Arduino Pro Mini v13
  J1 = LOAD_CELL [package=1x03]
  R2 = Resistor [tolerance=±5% resistance=1k package=THT]
  LED1 = RGB LED - (4 legs) [package="5 mm [THT]"]
  Part2 = Bluetooth HC-05 Macho
  VCC1 = Battery
  S1 = Round Pushbutton
  LED2 = RGB LED - (4 legs) [package="5 mm [THT]"]
  R3 = Resistor [tolerance=±5% resistance=1k package=THT]

nets:
  VCC: IC1.pin1, IC1.pin2, Part1.VCC, J1.B, R2.Pin_1, LED1.common_anode, Part2.VCC, S1.leg1, LED2.common_anode
  GND: IC1.pin3, IC1.pin5, IC1.pin12, Part1.GND, J1.R, Part2.GND, VCC1.-, R3.Pin_1
  N1: IC1.pin4, IC1.pin15
  N2: IC1.pin6, J1.W
  N3: IC1.pin7, R2.Pin_0, R3.Pin_0
  N4: IC1.pin8, R1.Pin_1
  N5: IC1.pin9, R1.Pin_0
  N6: IC1.pin10, IC1.pin11, Part1.A0
  N7: Part1.D9_PWM, LED1.blue_cathode, LED2.blue_cathode
  N8: Part1.D8, LED1.green_cathode, LED2.green_cathode
  N9: Part1.D7, LED1.red_cathode, LED2.red_cathode
  N10: Part1.D3_PWM, Part2.TXD
  N11: Part1.D2, Part2.RXD
  N12: VCC1.+, S1.leg0
